// Logisim project Lab9_Code_to_Gate_MaxSelector.circ as structural Verilog: 1 circuit, main circuit main
module main (
  input  [3:0] A,
  input  [3:0] B,
  output A_gt_B,
  output [3:0] C
);

  Comparator #(.width(4), .mode("unsigned")) comparator_1 (.a(A), .b(B), .gt(A_gt_B));  // open: eq, lt
  Multiplexer #(.select(1), .width(4)) multiplexer_1 (.in0(B), .in1(A), .out(C), .en(A_gt_B));  // open: sel

  // Notes on the sheet:
  //   A (a)
  //   B (b)
  //   MUX: sel=1 -> A, sel=0 -> B
  //   Lab 9: if (a > b) c = a; else c = b;   =>   Comparator + 2:1 MUX (4-bit)
endmodule
