// Logisim project smart_street_light_fsm.circ as structural Verilog: 1 circuit, main circuit main
module main (
  input  P__Pedestrian,
  input  T__Timer,
  input  C__Crossing_Timer
);

  wire and_1_out, and_2_out, and_3_out, and_4_out, CLOCK_out, D1, FF1__Q1_q, not_2_out, not_3_out, or_1_out,
       Q0, Q1bar, undriven;

  Clock CLOCK (.out(CLOCK_out));
  and and_1 (and_1_out, Q1bar, Q0, T__Timer);
  and and_2 (and_2_out, C__Crossing_Timer, D1);
  not not_1 (D1, undriven);
  not not_2 (not_2_out, P__Pedestrian);
  not not_3 (not_3_out, and_2_out);
  or or_1 (or_1_out, and_1_out, not_3_out);
  D_Flip_Flop FF1__Q1 (.clk(D1), .D(CLOCK_out), .Q(FF1__Q1_q), .Qn(Q1bar));  // open: preset, en, reset
  D_Flip_Flop FF0__Q0 (.clk(not_2_out), .D(CLOCK_out), .Q(Q0));  // open: Qn, preset, en, reset
  and and_3 (and_3_out, T__Timer, or_1_out);
  and and_4 (and_4_out, P__Pedestrian, Q0);
  LED Main_Green (.in(and_3_out));
  LED Main_Yellow (.in(and_4_out));
  LED Main_Red (.in(FF1__Q1_q));
  LED Ped_Green (.in(Q0));
  LED Ped_Red (.in(and_1_out));

  // Notes on the sheet:
  //   SMART STREET-LIGHT CONTROLLER FSM
endmodule
